# Fritzing sketch skema (saved by Fritzing 1.0.5)

parts:
  M1 = DOIT Esp32 DevKit v1 (30 pins long, 11 pins width) [part_number=ESP32S-PIN30]
  A1 = DFR0379
  A2 = AZDelivery 2channel solid state relay module
  M2 = TS-300B Controller [part_number=KIE-TS-300B]
  PH-4502C1 = PH-4502C [form="♀ (female)"]
  DS1 = DS18B20 1-Wire Temperature Sensor Probe
  J1 = Camdenboss CTB0158-2 [part_number=CTB0158-2 package=THT]
  J2 = Camdenboss CTB0158-2 [part_number=CTB0158-2 package=THT]
  J3 = Camdenboss CTB0158-2 [part_number=CTB0158-2 package=THT]

nets:
  VCC: M1.3V3, M2.Vcc, PH-4502C1.VCC, DS1.VDD
  GND: M1.GND, A1.Pin_7, A1.Pin_8, A2.Pin_2, M2.GND, PH-4502C1.GND, DS1.GND
  N1: M1.D4, DS1.DQ
  N2: M1.D34, PH-4502C1.Po
  N3: M1.D35, M2.ADC
  N4: M1.D27, A2.Pin_3
  N5: M1.VIN, A1.Pin_3, A1.Pin_6, A2.Pin_1, J1.pin2, J2.pin2, J3.pin1
  N6: A1.Pin_1, A1.Pin_2, J1.pin1, J2.pin1
  N7: A2.Pin_7, J3.pin2
  N8: A2.Pin_8, J1.terminal_1

notes:
  Water Heater
  ADAPTOR 12 Volt
  Socket Listrik 220Vac

custom parts:
  DOIT Esp32 DevKit v1 (30 pins long, 11 pins width): The DOIT Esp32 DevKit v1 is one of the development board created by DOIT to evaluate the ESP-WROOM-32 module. It is based on the ESP32 microcontroller that boasts Wifi, Bluetooth, Ethernet and Low Power support all in a single chip. (vanepp) made breadboard work, adjusted pin numbering and labels and reduced size of schematic and cleaned up pcb. This chip is 30pins long (2 x15) and 11 pins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
  DFR0379: 20W Adjustable DC-DC Buck Converter with Digital Display.
  AZDelivery 2channel solid state relay module: AZDelivery 2channel solid state relay module.
  TS-300B Controller: TS-300B Turbidity Sensor Controller The TS‑300B Turbidity Sensor is used to detect water quality by measuring the levels of turbidity or opaqueness. It uses light to detect suspended particles in water by measuring the light transmittance and scattering rate, which changes with the amount of Total Suspended Solids (TSS) in water. As the TTS increases the liquid turbidity level increases. This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
  PH-4502C: Shield for pH-Sensor PH0-14
